// Logisim project 16bitAdder.circ as structural Verilog
module halfAdder (
  input  in_1,
  input  in_2,
  output out_3,
  output out_4
);

  xor xor_1 (out_4, in_1, in_2);
  and and_1 (out_3, in_1, in_2);
endmodule

module Full_Adder (
  input  a,
  input  b,
  input  in_3,
  output Carry,
  output Sum
);

  wire halfadder_1_out_3, halfadder_1_out_4, halfadder_2_out_3;

  halfAdder halfadder_1 (.in_1(a), .in_2(b), .out_3(halfadder_1_out_3), .out_4(halfadder_1_out_4));
  halfAdder halfadder_2 (.in_1(halfadder_1_out_4), .in_2(in_3), .out_3(halfadder_2_out_3), .out_4(Sum));
  or or_1 (Carry, halfadder_1_out_3, halfadder_2_out_3);
endmodule

module _8_bit_Adder (
  input  [7:0] in_1,
  input  [7:0] in_2,
  input  in_3,
  output carry,
  output [7:0] out_5
);

  wire full_adder_1_carry, full_adder_2_carry, full_adder_3_carry, full_adder_4_carry, full_adder_5_carry,
       full_adder_6_carry, full_adder_7_carry;

  Full_Adder full_adder_1 (.a(in_1[0]), .b(in_2[0]), .in_3(in_3), .Carry(full_adder_1_carry), .Sum(out_5[0]));
  Full_Adder full_adder_2 (
    .a(in_1[1]), .b(in_2[1]), .in_3(full_adder_1_carry), .Carry(full_adder_2_carry), .Sum(out_5[1]));
  Full_Adder full_adder_3 (
    .a(in_1[2]), .b(in_2[2]), .in_3(full_adder_2_carry), .Carry(full_adder_3_carry), .Sum(out_5[2]));
  Full_Adder full_adder_4 (
    .a(in_1[3]), .b(in_2[3]), .in_3(full_adder_3_carry), .Carry(full_adder_4_carry), .Sum(out_5[3]));
  Full_Adder full_adder_5 (
    .a(in_1[4]), .b(in_2[4]), .in_3(full_adder_4_carry), .Carry(full_adder_5_carry), .Sum(out_5[4]));
  Full_Adder full_adder_6 (
    .a(in_1[5]), .b(in_2[5]), .in_3(full_adder_5_carry), .Carry(full_adder_6_carry), .Sum(out_5[5]));
  Full_Adder full_adder_7 (
    .a(in_1[6]), .b(in_2[6]), .in_3(full_adder_6_carry), .Carry(full_adder_7_carry), .Sum(out_5[6]));
  Full_Adder full_adder_8 (.a(in_1[7]), .b(in_2[7]), .in_3(full_adder_7_carry), .Carry(carry), .Sum(out_5[7]));
endmodule

module _16_bit_Adder (
  input  [15:0] in_1,
  input  [15:0] in_2,
  input  in_3,
  output out_4,
  output [15:0] out_5
);

  wire n8_bit_adder_1_carry;

  _8_bit_Adder u_8_bit_adder_1 (
    .in_1(in_1[7:0]), .in_2(in_2[7:0]), .in_3(in_3), .carry(n8_bit_adder_1_carry), .out_5(out_5[7:0]));
  _8_bit_Adder u_8_bit_adder_2 (
    .in_1(in_1[15:8]), .in_2(in_2[15:8]), .in_3(n8_bit_adder_1_carry), .carry(out_4), .out_5(out_5[15:8]));
endmodule
