// Logisim project ALU.circ as structural Verilog
module halfAdder (
  input  in_1,
  input  in_2,
  output out_3,
  output out_4
);

  xor xor_1 (out_4, in_1, in_2);
  and and_1 (out_3, in_1, in_2);
endmodule

module Full_Adder (
  input  a,
  input  b,
  input  in_3,
  output Carry,
  output Sum
);

  wire halfadder_1_out_3, halfadder_1_out_4, halfadder_2_out_3;

  halfAdder halfadder_1 (.in_1(a), .in_2(b), .out_3(halfadder_1_out_3), .out_4(halfadder_1_out_4));
  halfAdder halfadder_2 (.in_1(halfadder_1_out_4), .in_2(in_3), .out_3(halfadder_2_out_3), .out_4(Sum));
  or or_1 (Carry, halfadder_1_out_3, halfadder_2_out_3);
endmodule

module _8_bit_Adder (
  input  [7:0] in_1,
  input  [7:0] in_2,
  input  in_3,
  output carry,
  output [7:0] out_5
);

  wire full_adder_1_carry, full_adder_2_carry, full_adder_3_carry, full_adder_4_carry, full_adder_5_carry,
       full_adder_6_carry, full_adder_7_carry;

  Full_Adder full_adder_1 (.a(in_1[0]), .b(in_2[0]), .in_3(in_3), .Carry(full_adder_1_carry), .Sum(out_5[0]));
  Full_Adder full_adder_2 (
    .a(in_1[1]), .b(in_2[1]), .in_3(full_adder_1_carry), .Carry(full_adder_2_carry), .Sum(out_5[1]));
  Full_Adder full_adder_3 (
    .a(in_1[2]), .b(in_2[2]), .in_3(full_adder_2_carry), .Carry(full_adder_3_carry), .Sum(out_5[2]));
  Full_Adder full_adder_4 (
    .a(in_1[3]), .b(in_2[3]), .in_3(full_adder_3_carry), .Carry(full_adder_4_carry), .Sum(out_5[3]));
  Full_Adder full_adder_5 (
    .a(in_1[4]), .b(in_2[4]), .in_3(full_adder_4_carry), .Carry(full_adder_5_carry), .Sum(out_5[4]));
  Full_Adder full_adder_6 (
    .a(in_1[5]), .b(in_2[5]), .in_3(full_adder_5_carry), .Carry(full_adder_6_carry), .Sum(out_5[5]));
  Full_Adder full_adder_7 (
    .a(in_1[6]), .b(in_2[6]), .in_3(full_adder_6_carry), .Carry(full_adder_7_carry), .Sum(out_5[6]));
  Full_Adder full_adder_8 (.a(in_1[7]), .b(in_2[7]), .in_3(full_adder_7_carry), .Carry(carry), .Sum(out_5[7]));
endmodule

module _16_bit_Adder (
  input  [15:0] in_1,
  input  [15:0] in_2,
  input  in_3,
  output out_4,
  output [15:0] out_5
);

  wire n8_bit_adder_1_carry;

  _8_bit_Adder u_8_bit_adder_1 (
    .in_1(in_1[7:0]), .in_2(in_2[7:0]), .in_3(in_3), .carry(n8_bit_adder_1_carry), .out_5(out_5[7:0]));
  _8_bit_Adder u_8_bit_adder_2 (
    .in_1(in_1[15:8]), .in_2(in_2[15:8]), .in_3(n8_bit_adder_1_carry), .carry(out_4), .out_5(out_5[15:8]));
endmodule

module ALU (
  input  [2:0] ALUcontrol,
  input  SUBcontrol,
  input  [15:0] rt,
  input  [15:0] rs,
  output out_5,
  output [15:0] data,
  output brancheq,
  output overflowFlag
);

  wire and_1_out, and_3_out, and_4_out, and_5_out, and_6_out, not_2_out, not_3_out, not_4_out, not_6_out,
       or_2_out, xnor_1_out, xnor_2_out;
  wire [0:0] and_7_out;
  wire [15:0] and_2_out, multiplexer_1_out, n16_bit_adder_1_out_5, not_1_out, or_1_out;

  assign not_1_out = ~rt;  // NOT_Gate not_1, 16 bits wide
  xnor xnor_1 (xnor_1_out, rt[15], rs[15]);
  not not_2 (not_2_out, rt[15]);
  not not_3 (not_3_out, rs[15]);
  and and_1 (and_1_out, not_2_out, SUBcontrol, rs[15]);
  assign or_1_out = rt | rs;  // OR_Gate or_1, 16 bits wide
  assign and_2_out = rt & rs;  // AND_Gate and_2, 16 bits wide
  or or_2 (or_2_out, n16_bit_adder_1_out_5[0], n16_bit_adder_1_out_5[1], n16_bit_adder_1_out_5[2], n16_bit_adder_1_out_5[3], n16_bit_adder_1_out_5[4], n16_bit_adder_1_out_5[5], n16_bit_adder_1_out_5[6], n16_bit_adder_1_out_5[7], n16_bit_adder_1_out_5[9], n16_bit_adder_1_out_5[10], n16_bit_adder_1_out_5[11], n16_bit_adder_1_out_5[12], n16_bit_adder_1_out_5[13], n16_bit_adder_1_out_5[14], n16_bit_adder_1_out_5[15], n16_bit_adder_1_out_5[8]);
  not not_4 (not_4_out, n16_bit_adder_1_out_5[15]);
  and and_3 (and_3_out, rt[15], SUBcontrol, not_3_out);
  Multiplexer #(.width(16), .enable("false")) multiplexer_1 (
    .in0(rt), .in1(not_1_out), .out(multiplexer_1_out), .sel(SUBcontrol));
  _16_bit_Adder u_16_bit_adder_1 (
    .in_1(multiplexer_1_out), .in_2(rs), .in_3(SUBcontrol), .out_4(out_5), .out_5(n16_bit_adder_1_out_5));
  not not_5 (brancheq, or_2_out);
  not not_6 (not_6_out, SUBcontrol);
  xnor xnor_2 (xnor_2_out, n16_bit_adder_1_out_5[15], xnor_1_out);
  and and_4 (and_4_out, not_4_out, and_1_out);
  and and_5 (and_5_out, n16_bit_adder_1_out_5[15], and_3_out);
  and and_6 (and_6_out, not_6_out, xnor_2_out);
  Multiplexer #(.select(3), .width(16), .enable("false")) multiplexer_2 (
    .in0(and_2_out), .in1(or_1_out), .in2(n16_bit_adder_1_out_5),
    .in3({n16_bit_adder_1_out_5[15], {15{1'b0}}}), .in4({{15{1'b0}}, and_7_out[0]}), .out(data),
    .sel(ALUcontrol));  // open: in5, in6, in7
  or or_3 (overflowFlag, and_6_out, and_4_out, and_5_out);
  and and_7 (and_7_out[0], n16_bit_adder_1_out_5[15], SUBcontrol);
endmodule
