// Logisim project CPU.circ as structural Verilog: 8 circuits, main circuit main
module main (
  input  in_1,
  input  in_2,
  output out_3,
  output out_4
);

  xor xor_1 (out_4, in_1, in_2);
  and and_1 (out_3, in_1, in_2);
endmodule

module Half_Adder (
  input  a,
  input  b,
  input  in_3,
  output Carry,
  output Sum
);

  wire main_1_out_3, main_1_out_4, main_2_out_3;

  main main_1 (.in_1(a), .in_2(b), .out_3(main_1_out_3), .out_4(main_1_out_4));
  main main_2 (.in_1(main_1_out_4), .in_2(in_3), .out_3(main_2_out_3), .out_4(Sum));
  or or_1 (Carry, main_1_out_3, main_2_out_3);
endmodule

module _8__Bit_Adder (
  input  [7:0] in_1,
  input  [7:0] in_2,
  input  in_3,
  output carry,
  output [7:0] out_5
);

  wire half_adder_1_carry, half_adder_2_carry, half_adder_3_carry, half_adder_4_carry, half_adder_5_carry,
       half_adder_6_carry, half_adder_7_carry;

  Half_Adder half_adder_1 (.a(in_1[0]), .b(in_2[0]), .Carry(half_adder_1_carry), .Sum(out_5[0]), .in_3(in_3));
  Half_Adder half_adder_2 (
    .a(in_1[1]), .b(in_2[1]), .Carry(half_adder_2_carry), .Sum(out_5[1]), .in_3(half_adder_1_carry));
  Half_Adder half_adder_3 (
    .a(in_1[2]), .b(in_2[2]), .Carry(half_adder_3_carry), .Sum(out_5[2]), .in_3(half_adder_2_carry));
  Half_Adder half_adder_4 (
    .a(in_1[3]), .b(in_2[3]), .Carry(half_adder_4_carry), .Sum(out_5[3]), .in_3(half_adder_3_carry));
  Half_Adder half_adder_5 (
    .a(in_1[4]), .b(in_2[4]), .Carry(half_adder_5_carry), .Sum(out_5[4]), .in_3(half_adder_4_carry));
  Half_Adder half_adder_6 (
    .a(in_1[5]), .b(in_2[5]), .Carry(half_adder_6_carry), .Sum(out_5[5]), .in_3(half_adder_5_carry));
  Half_Adder half_adder_7 (
    .a(in_1[6]), .b(in_2[6]), .Carry(half_adder_7_carry), .Sum(out_5[6]), .in_3(half_adder_6_carry));
  Half_Adder half_adder_8 (.a(in_1[7]), .b(in_2[7]), .Carry(carry), .Sum(out_5[7]), .in_3(half_adder_7_carry));
endmodule

module ALU (
  input  [15:0] in_1,
  input  [15:0] in_2,
  input  in_3,
  output out_4,
  output [15:0] out_5
);

  wire n8_bit_adder_1_carry;

  _8__Bit_Adder u_8_bit_adder_1 (
    .in_1(in_1[7:0]), .in_2(in_2[7:0]), .in_3(in_3), .out_5(out_5[7:0]), .carry(n8_bit_adder_1_carry));
  _8__Bit_Adder u_8_bit_adder_2 (
    .in_1(in_1[15:8]), .in_2(in_2[15:8]), .in_3(n8_bit_adder_1_carry), .out_5(out_5[15:8]), .carry(out_4));
endmodule

module ALU2 (
  input  [2:0] ALUcontrol,
  input  SUBcontrol,
  input  [15:0] rt,
  input  [15:0] rs,
  output out_5,
  output [15:0] data,
  output brancheq,
  output overflowFlag
);

  wire and_1_out, and_3_out, and_4_out, and_5_out, and_6_out, not_2_out, not_3_out, not_4_out, not_6_out,
       or_2_out, xnor_1_out, xnor_2_out;
  wire [0:0] and_7_out;
  wire [14:0] alu_1_out_5_2;
  wire [15:0] and_2_out, multiplexer_1_out, not_1_out, or_1_out;
  wire [15:15] alu_1_out_5;

  assign not_1_out = ~rt;  // NOT_Gate not_1, 16 bits wide
  xnor xnor_1 (xnor_1_out, rt[15], rs[15]);
  not not_2 (not_2_out, rt[15]);
  not not_3 (not_3_out, rs[15]);
  and and_1 (and_1_out, not_2_out, SUBcontrol, rs[15]);
  assign or_1_out = rt | rs;  // OR_Gate or_1, 16 bits wide
  assign and_2_out = rt & rs;  // AND_Gate and_2, 16 bits wide
  or or_2 (or_2_out, alu_1_out_5_2[0], alu_1_out_5_2[1], alu_1_out_5_2[2], alu_1_out_5_2[3], alu_1_out_5_2[4], alu_1_out_5_2[5], alu_1_out_5_2[6], alu_1_out_5_2[7], alu_1_out_5_2[9], alu_1_out_5_2[10], alu_1_out_5_2[11], alu_1_out_5_2[12], alu_1_out_5_2[13], alu_1_out_5_2[14], alu_1_out_5[15], alu_1_out_5_2[8]);
  not not_4 (not_4_out, alu_1_out_5[15]);
  and and_3 (and_3_out, rt[15], SUBcontrol, not_3_out);
  Multiplexer #(.width(16), .enable("false")) multiplexer_1 (
    .in0(rt), .in1(not_1_out), .out(multiplexer_1_out), .sel(SUBcontrol));
  ALU alu_1 (
    .in_1(multiplexer_1_out), .in_2(rs), .in_3(SUBcontrol), .out_4(out_5),
    .out_5({alu_1_out_5[15], alu_1_out_5_2}));
  not not_5 (brancheq, or_2_out);
  not not_6 (not_6_out, SUBcontrol);
  xnor xnor_2 (xnor_2_out, alu_1_out_5[15], xnor_1_out);
  and and_4 (and_4_out, not_4_out, and_1_out);
  and and_5 (and_5_out, alu_1_out_5[15], and_3_out);
  and and_6 (and_6_out, not_6_out, xnor_2_out);
  Multiplexer #(.select(3), .width(16), .enable("false")) multiplexer_2 (
    .in0(and_2_out), .in1(or_1_out), .in2({alu_1_out_5[15], alu_1_out_5_2}),
    .in3({alu_1_out_5[15], {15{1'b0}}}), .in4({{15{1'b0}}, and_7_out[0]}), .out(data), .sel(ALUcontrol));  // open: in5, in6, in7
  or or_3 (overflowFlag, and_6_out, and_4_out, and_5_out);
  and and_7 (and_7_out[0], alu_1_out_5[15], SUBcontrol);
endmodule

module register (
  input  writeEnable,
  input  clk,
  input  [2:0] reg1Addr,
  input  [2:0] writeReg,
  input  [2:0] reg2Addr,
  input  [15:0] data,
  input  in_7,
  output [15:0] reg1data,
  output [15:0] reg2data
);

  wire decoder_1_out0, decoder_1_out1, decoder_1_out2, decoder_1_out3, decoder_1_out4, decoder_1_out5,
       decoder_1_out6, decoder_1_out7;
  wire [15:0] controlled_buffer_1_out, controlled_buffer_2_out, controlled_buffer_3_out,
       controlled_buffer_4_out, controlled_buffer_5_out, controlled_buffer_6_out, controlled_buffer_7_out,
       controlled_buffer_8_out, register_1_q, register_2_q, register_3_q, register_4_q, register_5_q,
       register_6_q, register_7_q, register_8_q;

  Decoder #(.select(3), .enable("false")) decoder_1 (
    .out0(decoder_1_out0), .out1(decoder_1_out1), .out2(decoder_1_out2), .out3(decoder_1_out3),
    .out4(decoder_1_out4), .out5(decoder_1_out5), .out6(decoder_1_out6), .out7(decoder_1_out7), .sel(writeReg));
  Register #(.width(16)) register_1 (
    .D(controlled_buffer_1_out), .en(decoder_1_out0), .Q(register_1_q), .clk(clk), .clr(in_7));
  assign controlled_buffer_1_out = writeEnable ? data : 16'bz;  // Controlled_Buffer controlled_buffer_1
  assign controlled_buffer_2_out = writeEnable ? data : 16'bz;  // Controlled_Buffer controlled_buffer_2
  Register #(.width(16)) register_2 (
    .D(controlled_buffer_2_out), .en(decoder_1_out1), .Q(register_2_q), .clk(clk), .clr(in_7));
  assign controlled_buffer_3_out = writeEnable ? data : 16'bz;  // Controlled_Buffer controlled_buffer_3
  Register #(.width(16)) register_3 (
    .D(controlled_buffer_3_out), .en(decoder_1_out2), .Q(register_3_q), .clk(clk), .clr(in_7));
  Register #(.width(16)) register_4 (
    .D(controlled_buffer_4_out), .en(decoder_1_out3), .Q(register_4_q), .clk(clk), .clr(in_7));
  assign controlled_buffer_4_out = writeEnable ? data : 16'bz;  // Controlled_Buffer controlled_buffer_4
  assign controlled_buffer_5_out = writeEnable ? data : 16'bz;  // Controlled_Buffer controlled_buffer_5
  Register #(.width(16)) register_5 (
    .D(controlled_buffer_5_out), .en(decoder_1_out4), .Q(register_5_q), .clk(clk), .clr(in_7));
  assign controlled_buffer_6_out = writeEnable ? data : 16'bz;  // Controlled_Buffer controlled_buffer_6
  Register #(.width(16)) register_6 (
    .D(controlled_buffer_6_out), .en(decoder_1_out5), .Q(register_6_q), .clk(clk), .clr(in_7));
  Register #(.width(16)) register_7 (
    .D(controlled_buffer_7_out), .en(decoder_1_out6), .Q(register_7_q), .clk(clk), .clr(in_7));
  assign controlled_buffer_7_out = writeEnable ? data : 16'bz;  // Controlled_Buffer controlled_buffer_7
  Register #(.width(16)) register_8 (
    .D(controlled_buffer_8_out), .en(decoder_1_out7), .Q(register_8_q), .clk(clk), .clr(in_7));
  assign controlled_buffer_8_out = writeEnable ? data : 16'bz;  // Controlled_Buffer controlled_buffer_8
  Multiplexer #(.select(3), .width(16), .enable("false")) multiplexer_1 (
    .in0(register_1_q), .in1(register_2_q), .in2(register_3_q), .in3(register_4_q), .in4(register_5_q),
    .in5(register_6_q), .in6(register_7_q), .in7(register_8_q), .out(reg1data), .sel(reg1Addr));
  Multiplexer #(.select(3), .width(16), .enable("false")) multiplexer_2 (
    .in0(register_1_q), .in1(register_2_q), .in2(register_3_q), .in3(register_4_q), .in4(register_5_q),
    .in5(register_6_q), .in6(register_7_q), .in7(register_8_q), .out(reg2data), .sel(reg2Addr));
endmodule

module controlUnit (
  input  [15:0] in_1,
  output [2:0] ALUcontorl,
  output SUB_contorl,
  output jr,
  output rd,
  output addi,
  output branchequal,
  output jal,
  output immediate,
  output writeEnablee,
  output lw,
  output sw,
  output out_13
);

  wire and_1_out, and_2_out, and_3_out, and_4_out, and_5_out, decoder_1_out0, decoder_1_out1, decoder_1_out2,
       decoder_2_out0, decoder_2_out1, decoder_2_out2, decoder_2_out3, decoder_2_out4, decoder_2_out8,
       or_4_out, or_5_out, or_6_out, or_7_out;
  wire [2:0] priority_encoder_1_out;

  Decoder #(.select(3), .enable("false")) decoder_1 (
    .out0(decoder_1_out0), .out1(decoder_1_out1), .out2(decoder_1_out2), .out3(jal), .out4(lw), .out5(sw),
    .out6(branchequal), .out7(addi), .sel(in_1[15:13]));
  or or_1 (rd, in_1[15], in_1[14], in_1[13]);
  Decoder #(.select(4), .enable("false")) decoder_2 (
    .out0(decoder_2_out0), .out1(decoder_2_out1), .out2(decoder_2_out2), .out3(decoder_2_out3),
    .out4(decoder_2_out4), .out8(decoder_2_out8), .sel(in_1[3:0]));  // open: out5, out6, out7, out9, out10, out11, out12, out13, out14, out15
  or or_2 (out_13, decoder_1_out2, jal);
  and and_1 (and_1_out, decoder_1_out0, decoder_2_out0);
  and and_2 (and_2_out, decoder_1_out0, decoder_2_out1);
  and and_3 (and_3_out, decoder_2_out2, decoder_1_out0);
  and and_4 (and_4_out, decoder_1_out0, decoder_2_out3);
  and and_5 (and_5_out, decoder_1_out0, decoder_2_out4);
  and and_6 (jr, decoder_2_out8, decoder_1_out0);
  or or_3 (immediate, addi, lw, sw, decoder_1_out1);
  or or_4 (or_4_out, and_2_out, branchequal);
  or or_5 (or_5_out, and_1_out, or_4_out, sw, addi, lw);
  or or_6 (or_6_out, and_5_out, decoder_1_out1);
  Multiplexer #(.select(3), .width(3), .enable("false")) multiplexer_1 (
    .in0(3'b000), .in1(3'b001), .in2(3'b010), .in3(3'b011), .in4(3'b100), .out(ALUcontorl),
    .sel(priority_encoder_1_out));  // open: in5, in6, in7
  Priority_Encoder priority_encoder_1 (
    .in0(and_3_out), .in1(and_4_out), .in2(or_5_out), .in3(branchequal), .in4(or_6_out),
    .out(priority_encoder_1_out));  // open: in5, in6, in7, en_in, gs, en_out
  Multiplexer #(.enable("false")) multiplexer_2 (.in0(1'b0), .in1(1'b1), .out(SUB_contorl), .sel(or_7_out));
  or or_7 (or_7_out, or_4_out, and_5_out, decoder_1_out1);
  nor nor_1 (writeEnablee, jr, sw, branchequal, decoder_1_out2);

  // Notes on the sheet:
  //   j
  //   add
  //   beq
  //   sub
  //   and
  //   or
  //   slt
  //   slti
endmodule

module CPU (
  input  in_1,
  output overFlowFlag
);

  wire alu2_1_brancheq, and_1_out, clock_1_out, controlunit_1_branchequal, controlunit_1_immediate,
       controlunit_1_jal, controlunit_1_jr, controlunit_1_lw, controlunit_1_out_13, controlunit_1_rd,
       controlunit_1_sub_contorl, controlunit_1_sw, controlunit_1_writeenablee;
  wire [2:0] controlunit_1_alucontorl, multiplexer_4_out, multiplexer_5_out;
  wire [12:0] ram_1_data;
  wire [15:0] alu2_1_data, alu_1_out_5, alu_2_out_5, alu_3_out_5, multiplexer_1_out, multiplexer_2_out,
       multiplexer_3_out, multiplexer_6_out, multiplexer_7_out, multiplexer_8_out, ram_2_data, register_1_q,
       register_2_reg1data, register_2_reg2data;
  wire [15:13] ram_1_data_2;

  Multiplexer #(.width(16), .enable("false")) multiplexer_1 (
    .in0(multiplexer_2_out), .in1({3'b000, ram_1_data}), .out(multiplexer_1_out), .sel(controlunit_1_out_13));
  ALU alu_1 (.in_1(alu_2_out_5), .in_2({{9{1'b0}}, ram_1_data[6:0]}), .in_3(1'b0), .out_5(alu_1_out_5));  // open: out_4
  Multiplexer #(.width(16), .enable("false")) multiplexer_2 (
    .in0(multiplexer_3_out), .in1(alu_1_out_5), .out(multiplexer_2_out), .sel(and_1_out));
  ALU alu_2 (.in_1({16{1'b0}}), .in_2(register_1_q), .in_3(1'b1), .out_5(alu_2_out_5));  // open: out_4
  Register #(.width(16)) register_1 (.D(multiplexer_1_out), .Q(register_1_q), .clk(clock_1_out));  // open: en, clr
  Clock clock_1 (.out(clock_1_out));
  Multiplexer #(.width(16), .enable("false")) multiplexer_3 (
    .in0(alu_2_out_5), .in1(register_2_reg1data), .out(multiplexer_3_out), .sel(controlunit_1_jr));
  and and_1 (and_1_out, controlunit_1_branchequal, alu2_1_brancheq);
  RAM #(.addrWidth(16), .dataWidth(16), .bus("separate")) ram_1 (
    .addr(register_1_q), .data({ram_1_data_2, ram_1_data}), .clk(clock_1_out));  // open: din, str, sel, ld, clr
  Multiplexer #(.width(3), .disabled(0), .enable("false")) multiplexer_4 (
    .in0(ram_1_data[6:4]), .in1(ram_1_data[9:7]), .out(multiplexer_4_out), .sel(controlunit_1_rd));
  Multiplexer #(.width(3), .disabled(0), .enable("false")) multiplexer_5 (
    .in0(multiplexer_4_out), .in1(3'b111), .out(multiplexer_5_out), .sel(controlunit_1_jal));
  controlUnit controlunit_1 (
    .in_1({ram_1_data_2, ram_1_data}), .ALUcontorl(controlunit_1_alucontorl),
    .SUB_contorl(controlunit_1_sub_contorl), .jal(controlunit_1_jal), .sw(controlunit_1_sw),
    .out_13(controlunit_1_out_13), .immediate(controlunit_1_immediate),
    .branchequal(controlunit_1_branchequal), .rd(controlunit_1_rd), .lw(controlunit_1_lw),
    .jr(controlunit_1_jr), .writeEnablee(controlunit_1_writeenablee));  // open: addi
  register register_2 (
    .writeEnable(controlunit_1_writeenablee), .reg1Addr(ram_1_data[12:10]), .writeReg(multiplexer_5_out),
    .reg2Addr(ram_1_data[9:7]), .data(multiplexer_8_out), .reg1data(register_2_reg1data),
    .reg2data(register_2_reg2data), .clk(clock_1_out), .in_7(in_1));
  Multiplexer #(.width(16), .enable("false")) multiplexer_6 (
    .in0(register_2_reg2data), .in1({{9{1'b0}}, ram_1_data[6:0]}), .out(multiplexer_6_out),
    .sel(controlunit_1_immediate));
  Multiplexer #(.width(16), .enable("false")) multiplexer_7 (
    .in0(alu2_1_data), .in1(ram_2_data), .out(multiplexer_7_out), .sel(controlunit_1_lw));
  Multiplexer #(.width(16), .enable("false")) multiplexer_8 (
    .in0(multiplexer_7_out), .in1(alu_3_out_5), .out(multiplexer_8_out), .sel(controlunit_1_jal));
  ALU alu_3 (.in_1({16{1'b0}}), .in_2(alu_2_out_5), .in_3(1'b1), .out_5(alu_3_out_5));  // open: out_4
  ALU2 alu2_1 (
    .ALUcontrol(controlunit_1_alucontorl), .SUBcontrol(controlunit_1_sub_contorl), .rt(multiplexer_6_out),
    .rs(register_2_reg1data), .data(alu2_1_data), .brancheq(alu2_1_brancheq), .overflowFlag(overFlowFlag));  // open: out_5
  RAM #(.addrWidth(16), .dataWidth(16), .bus("separate")) ram_2 (
    .addr(alu2_1_data), .din(register_2_reg2data), .data(ram_2_data), .str(controlunit_1_sw),
    .clk(clock_1_out));  // open: sel, ld, clr

  // Notes on the sheet:
  //   PC
  //   CLK
  //   64 KB Instruction Mem
  //   rd
  //   rt
  //   Control Unit
  //   Register
  //   Signextender
  //   ALU
  //   64 KB RAM
endmodule
