// Logisim project FullAdder.circ as structural Verilog
module halfAdder (
  input  in_1,
  input  in_2,
  output out_3,
  output out_4
);

  xor xor_1 (out_4, in_1, in_2);
  and and_1 (out_3, in_1, in_2);
endmodule

module Full_Adder (
  input  a,
  input  b,
  input  in_3,
  output Carry,
  output Sum
);

  wire halfadder_1_out_3, halfadder_1_out_4, halfadder_2_out_3;

  halfAdder halfadder_1 (.in_1(a), .in_2(b), .out_3(halfadder_1_out_3), .out_4(halfadder_1_out_4));
  halfAdder halfadder_2 (.in_1(halfadder_1_out_4), .in_2(in_3), .out_3(halfadder_2_out_3), .out_4(Sum));
  or or_1 (Carry, halfadder_1_out_3, halfadder_2_out_3);
endmodule
