// Logisim project controlUnit.circ as structural Verilog: 1 circuit, main circuit main
module main (
  input  [15:0] in_1,
  output [2:0] ALUcontorl,
  output SUB_contorl,
  output jr,
  output rd,
  output addi,
  output branchequal,
  output jal,
  output immediate,
  output writeEnablee,
  output lw,
  output sw,
  output out_13
);

  wire and_1_out, and_2_out, and_3_out, and_4_out, and_5_out, decoder_1_out0, decoder_1_out1, decoder_1_out2,
       decoder_2_out0, decoder_2_out1, decoder_2_out2, decoder_2_out3, decoder_2_out4, decoder_2_out8,
       or_4_out, or_5_out, or_6_out, or_7_out;
  wire [2:0] priority_encoder_1_out;

  Decoder #(.select(3), .enable("false")) decoder_1 (
    .out0(decoder_1_out0), .out1(decoder_1_out1), .out2(decoder_1_out2), .out3(jal), .out4(lw), .out5(sw),
    .out6(branchequal), .out7(addi), .sel(in_1[15:13]));
  or or_1 (rd, in_1[15], in_1[14], in_1[13]);
  Decoder #(.select(4), .enable("false")) decoder_2 (
    .out0(decoder_2_out0), .out1(decoder_2_out1), .out2(decoder_2_out2), .out3(decoder_2_out3),
    .out4(decoder_2_out4), .out8(decoder_2_out8), .sel(in_1[3:0]));  // open: out5, out6, out7, out9, out10, out11, out12, out13, out14, out15
  or or_2 (out_13, decoder_1_out2, jal);
  and and_1 (and_1_out, decoder_1_out0, decoder_2_out0);
  and and_2 (and_2_out, decoder_1_out0, decoder_2_out1);
  and and_3 (and_3_out, decoder_2_out2, decoder_1_out0);
  and and_4 (and_4_out, decoder_1_out0, decoder_2_out3);
  and and_5 (and_5_out, decoder_1_out0, decoder_2_out4);
  and and_6 (jr, decoder_2_out8, decoder_1_out0);
  or or_3 (immediate, addi, lw, sw, decoder_1_out1);
  or or_4 (or_4_out, and_2_out, branchequal);
  or or_5 (or_5_out, and_1_out, or_4_out, sw, addi, lw);
  or or_6 (or_6_out, and_5_out, decoder_1_out1);
  Multiplexer #(.select(3), .width(3), .enable("false")) multiplexer_1 (
    .in0(3'b000), .in1(3'b001), .in2(3'b010), .in3(3'b011), .in4(3'b100), .out(ALUcontorl),
    .sel(priority_encoder_1_out));  // open: in5, in6, in7
  Priority_Encoder priority_encoder_1 (
    .in0(and_3_out), .in1(and_4_out), .in2(or_5_out), .in3(branchequal), .in4(or_6_out),
    .out(priority_encoder_1_out));  // open: in5, in6, in7, en_in, gs, en_out
  Multiplexer #(.enable("false")) multiplexer_2 (.in0(1'b0), .in1(1'b1), .out(SUB_contorl), .sel(or_7_out));
  or or_7 (or_7_out, or_4_out, and_5_out, decoder_1_out1);
  nor nor_1 (writeEnablee, jr, sw, branchequal, decoder_1_out2);

  // Notes on the sheet:
  //   j
  //   add
  //   beq
  //   sub
  //   and
  //   or
  //   slt
  //   slti
endmodule
