// Logisim project register.circ as structural Verilog: 1 circuit, main circuit main
module main (
  input  writeEnable,
  input  clk,
  input  [2:0] reg1Addr,
  input  [2:0] writeReg,
  input  [2:0] reg2Addr,
  input  [15:0] data,
  input  in_7,
  output [15:0] reg1data,
  output [15:0] reg2data
);

  wire decoder_1_out0, decoder_1_out1, decoder_1_out2, decoder_1_out3, decoder_1_out4, decoder_1_out5,
       decoder_1_out6, decoder_1_out7;
  wire [15:0] controlled_buffer_1_out, controlled_buffer_2_out, controlled_buffer_3_out,
       controlled_buffer_4_out, controlled_buffer_5_out, controlled_buffer_6_out, controlled_buffer_7_out,
       controlled_buffer_8_out, register_1_q, register_2_q, register_3_q, register_4_q, register_5_q,
       register_6_q, register_7_q, register_8_q;

  Decoder #(.select(3), .enable("false")) decoder_1 (
    .out0(decoder_1_out0), .out1(decoder_1_out1), .out2(decoder_1_out2), .out3(decoder_1_out3),
    .out4(decoder_1_out4), .out5(decoder_1_out5), .out6(decoder_1_out6), .out7(decoder_1_out7), .sel(writeReg));
  Register #(.width(16)) register_1 (
    .D(controlled_buffer_1_out), .en(decoder_1_out0), .Q(register_1_q), .clk(clk), .clr(in_7));
  assign controlled_buffer_1_out = writeEnable ? data : 16'bz;  // Controlled_Buffer controlled_buffer_1
  Register #(.width(16)) register_2 (
    .D(controlled_buffer_2_out), .en(decoder_1_out1), .Q(register_2_q), .clk(clk), .clr(in_7));
  assign controlled_buffer_2_out = writeEnable ? data : 16'bz;  // Controlled_Buffer controlled_buffer_2
  Register #(.width(16)) register_3 (
    .D(controlled_buffer_3_out), .en(decoder_1_out2), .Q(register_3_q), .clk(clk), .clr(in_7));
  assign controlled_buffer_3_out = writeEnable ? data : 16'bz;  // Controlled_Buffer controlled_buffer_3
  Register #(.width(16)) register_4 (
    .D(controlled_buffer_4_out), .en(decoder_1_out3), .Q(register_4_q), .clk(clk), .clr(in_7));
  assign controlled_buffer_4_out = writeEnable ? data : 16'bz;  // Controlled_Buffer controlled_buffer_4
  assign controlled_buffer_5_out = writeEnable ? data : 16'bz;  // Controlled_Buffer controlled_buffer_5
  Register #(.width(16)) register_5 (
    .D(controlled_buffer_5_out), .en(decoder_1_out4), .Q(register_5_q), .clk(clk), .clr(in_7));
  Register #(.width(16)) register_6 (
    .D(controlled_buffer_6_out), .en(decoder_1_out5), .Q(register_6_q), .clk(clk), .clr(in_7));
  assign controlled_buffer_6_out = writeEnable ? data : 16'bz;  // Controlled_Buffer controlled_buffer_6
  assign controlled_buffer_7_out = writeEnable ? data : 16'bz;  // Controlled_Buffer controlled_buffer_7
  Register #(.width(16)) register_7 (
    .D(controlled_buffer_7_out), .en(decoder_1_out6), .Q(register_7_q), .clk(clk), .clr(in_7));
  Register #(.width(16)) register_8 (
    .D(controlled_buffer_8_out), .en(decoder_1_out7), .Q(register_8_q), .clk(clk), .clr(in_7));
  assign controlled_buffer_8_out = writeEnable ? data : 16'bz;  // Controlled_Buffer controlled_buffer_8
  Multiplexer #(.select(3), .width(16), .enable("false")) multiplexer_1 (
    .in0(register_1_q), .in1(register_2_q), .in2(register_3_q), .in3(register_4_q), .in4(register_5_q),
    .in5(register_6_q), .in6(register_7_q), .in7(register_8_q), .out(reg1data), .sel(reg1Addr));
  Multiplexer #(.select(3), .width(16), .enable("false")) multiplexer_2 (
    .in0(register_1_q), .in1(register_2_q), .in2(register_3_q), .in3(register_4_q), .in4(register_5_q),
    .in5(register_6_q), .in6(register_7_q), .in7(register_8_q), .out(reg2data), .sel(reg2Addr));
endmodule
